# Fritzing sketch Mp3Doorbell (saved by Fritzing 0.9.2b)

parts:
  Wifi = ESP8266 WiFi Module [part_number=ESP8266]
  Composant1 = Arduino Nano (Rev3.0)
  Mp3_Player = WTV020SD [package=ssop_20]
  To_Sound_system = Audio Jack (TRS) 3.5mm [package="PG203J [THT]"]
  S2 = Round Pushbutton  # not connected
  S3 = Round Pushbutton  # not connected
  16v_input = Power plug
  16v_to_9v = Voltage Regulator - Variable [package="TO220 [THT]"]
  U1 = Voltage Regulator - 3.3V [package="TO220 [THT]"]

nets:
  N1: Wifi.RXD, Composant1.D1/TX
  N2: Wifi.VCC, U1.output_voltage
  GND: Wifi.GND, Composant1.GND, Mp3_Player.GND, To_Sound_system.Sleeve, 16v_input.GND, U1.GND
  N3: Wifi.TXD, Composant1.D0/RX
  5V: Composant1.5V, Mp3_Player.VCC
  N4: Mp3_Player.SPK_P, To_Sound_system.Ring
  N5: Mp3_Player.SPK_N, To_Sound_system.Tip
  N6: 16v_input.VCC, 16v_to_9v.IN, U1.input_voltage

custom parts:
  ESP8266 WiFi Module: Generic WiFi Module based on the ESP8266 with onboard PCB antenna and UART communications
