# Fritzing sketch PiezoDrumLEDModule1 (saved by Fritzing 0.9.2b)
circuit board: 10cm x 5cm
breadboards: 1

parts:
  U1 = atmega328 [package=dip]
  J2 = Power Jack [package=power_jack_combo]
  DIN1 = DIN-5 jack (MIDI) [package=THT]
  DIN2 = DIN-5 jack (MIDI) [package=THT]
  DIN3 = DIN-5 jack (MIDI) [package=THT]
  J3 = AVR ISP 6 Pin [package=2x3_lock]
  JP1 = Header 2 [package=jst-2-pth]
  JP2 = Header 2 [package=jst-2-pth]
  JP3 = Header 2 [package=jst-2-pth]
  JP4 = Header 2 [package=jst-2-pth]

nets:
  N1: U1.D2, DIN1.2
  N2: U1.D3_(PWM), DIN3.2
  N3: U1.D4, DIN2.2
  N4: U1.VCC, J2.PWR, DIN1.1, DIN2.1, DIN3.1
  N5: U1.GND#7, J2.GND, DIN1.4, DIN2.4, DIN3.4
  N6: U1.D7, JP2.1
  N7: U1.D8, JP1.1
  N8: U1.D12, JP4.1
  N9: U1.D13, JP3.1
  N10: U1.AREF, JP1.2, JP2.2, JP3.2, JP4.2
  N11: U1.GND#21, J3.6
  N12: U1.A1, J3.1
  N13: U1.A2, J3.3
  N14: U1.A3, DIN2.3
  N15: U1.A4, DIN3.3
  N16: U1.A5, DIN1.3
