# Fritzing sketch 74HC595 Module-PCBNG-smd (saved by Fritzing 0.9.2b)
circuit board: 2.6671cm x 4.43727cm
breadboards: 1

parts:
  74HC595 = 74HC595 [package="DIP16 [THT]"]
  LED18 = LED - 3mm [color="Red (633nm)" package="3 mm [THT]"]
  LED19 = LED - 3mm [color="Red (633nm)" package="3 mm [THT]"]
  LED20 = LED - 3mm [color="Red (633nm)" package="3 mm [THT]"]
  LED23 = LED - 3mm [color="Red (633nm)" package="3 mm [THT]"]
  LED24 = LED - 3mm [color="Red (633nm)" package="3 mm [THT]"]
  LED21 = LED - 3mm [color="Red (633nm)" package="3 mm [THT]"]
  LED22 = LED - 3mm [color="Red (633nm)" package="3 mm [THT]"]
  LED17 = LED - 3mm [color="Red (633nm)" package="3 mm [THT]"]
  Input = female pin header, 5 pins [form="♀ (female)"]
  Link_output = female pin header, 5 pins [form="♀ (female)"]
  R16 = Resistor [tolerance=±5% resistance=220 package="0603 [SMD]"]
  R15 = Resistor [tolerance=±5% resistance=220 package="0603 [SMD]"]
  R14 = Resistor [tolerance=±5% resistance=220 package="0603 [SMD]"]
  R13 = Resistor [tolerance=±5% resistance=220 package="0603 [SMD]"]
  R12 = Resistor [tolerance=±5% resistance=220 package="0603 [SMD]"]
  R11 = Resistor [tolerance=±5% resistance=220 package="0603 [SMD]"]
  R10 = Resistor [tolerance=±5% resistance=220 package="0603 [SMD]"]
  R17 = Resistor [tolerance=±5% resistance=220 package="0603 [SMD]"]

nets:
  N1: 74HC595.Q1, LED18.anode
  N2: 74HC595.Q2, LED19.anode
  N3: 74HC595.Q3, LED20.anode
  N4: 74HC595.Q4, LED21.anode
  N5: 74HC595.Q5, LED22.anode
  N6: 74HC595.Q6, LED23.anode
  N7: 74HC595.Q7, LED24.anode
  N8: 74HC595.GND, 74HC595.OE, Input.pin4, Link_output.pin3, R16.Pin_1, R15.Pin_1, R14.Pin_0, R13.Pin_0, R12.Pin_0, R11.Pin_0, R10.Pin_0, R17.Pin_0
  N9: 74HC595.Q7', Link_output.pin2
  N10: 74HC595.SH_CP, Input.pin1, Link_output.pin5
  N11: 74HC595.ST_CP, Input.pin2, Link_output.pin4
  N12: 74HC595.DS, Input.pin3
  N13: 74HC595.Q0, LED17.anode
  N14: 74HC595.VCC, Input.pin5, Link_output.pin1
  N15: LED18.cathode, R15.Pin_0
  N16: LED19.cathode, R14.Pin_1
  N17: LED20.cathode, R13.Pin_1
  N18: LED23.cathode, R10.Pin_1
  N19: LED24.cathode, R17.Pin_1
  N20: LED21.cathode, R12.Pin_1
  N21: LED22.cathode, R11.Pin_1
  N22: LED17.cathode, R16.Pin_0

notes:
  VCC
  data
  GRND
  latch
  clock
