# Fritzing sketch 74HC595 Module-PCBNG (saved by Fritzing 0.9.3b)
circuit board: 3.79059cm x 6.14252cm
breadboards: 1

parts:
  74HC595 = 74HC595 [package="DIP16 [THT]"]
  R17 = Resistor [tolerance=±5% resistance=220 package=THT]
  R10 = Resistor [tolerance=±5% resistance=220 package=THT]
  R11 = Resistor [tolerance=±5% resistance=220 package=THT]
  R12 = Resistor [tolerance=±5% resistance=220 package=THT]
  R13 = Resistor [tolerance=±5% resistance=220 package=THT]
  R14 = Resistor [tolerance=±5% resistance=220 package=THT]
  R15 = Resistor [tolerance=±5% resistance=220 package=THT]
  R16 = Resistor [tolerance=±5% resistance=220 package=THT]
  LED18 = LED - 3mm [color="Red (633nm)" package="3 mm [THT]"]
  LED19 = LED - 3mm [color="Red (633nm)" package="3 mm [THT]"]
  LED20 = LED - 3mm [color="Red (633nm)" package="3 mm [THT]"]
  LED23 = LED - 3mm [color="Red (633nm)" package="3 mm [THT]"]
  LED24 = LED - 3mm [color="Red (633nm)" package="3 mm [THT]"]
  LED21 = LED - 3mm [color="Red (633nm)" package="3 mm [THT]"]
  LED22 = LED - 3mm [color="Red (633nm)" package="3 mm [THT]"]
  LED17 = LED - 3mm [color="Red (633nm)" package="3 mm [THT]"]
  Input = female pin header, 5 pins [form="♀ (female)"]
  Link_output = female pin header, 5 pins [form="♀ (female)"]

nets:
  N1: 74HC595.Q1, LED18.anode
  N2: 74HC595.Q2, LED19.anode
  N3: 74HC595.Q3, LED20.anode
  N4: 74HC595.Q4, LED21.anode
  N5: 74HC595.Q5, LED22.anode
  N6: 74HC595.Q6, LED23.anode
  N7: 74HC595.Q7, LED24.anode
  N8: 74HC595.GND, 74HC595.OE, R17.Pin_0, R10.Pin_0, R11.Pin_0, R12.Pin_0, R13.Pin_0, R14.Pin_0, R15.Pin_0, R16.Pin_0, Input.pin3, Link_output.pin3
  N9: 74HC595.Q7', Link_output.pin2
  N10: 74HC595.MR, 74HC595.VCC, Input.pin5, Link_output.pin1
  N11: 74HC595.SH_CP, Input.pin1, Link_output.pin5
  N12: 74HC595.ST_CP, Input.pin2, Link_output.pin4
  N13: 74HC595.DS, Input.pin4
  N14: 74HC595.Q0, LED17.anode
  N15: R17.Pin_1, LED24.cathode
  N16: R10.Pin_1, LED23.cathode
  N17: R11.Pin_1, LED22.cathode
  N18: R12.Pin_1, LED21.cathode
  N19: R13.Pin_1, LED20.cathode
  N20: R14.Pin_1, LED19.cathode
  N21: R15.Pin_1, LED18.cathode
  N22: R16.Pin_1, LED17.cathode

notes:
  VCC
  data
  GRND
  latch
  clock
