# Fritzing sketch 74HC595 Module (saved by Fritzing 0.9.2b)
circuit board: 3.62918cm x 6.35944cm
breadboards: 1

parts:
  U1 = 74HC595 [package="DIP16 [THT]"]
  R17 = Resistor [tolerance=±5% resistance=220 package=THT]
  R10 = Resistor [tolerance=±5% resistance=220 package=THT]
  R11 = Resistor [tolerance=±5% resistance=220 package=THT]
  R12 = Resistor [tolerance=±5% resistance=220 package=THT]
  R13 = Resistor [tolerance=±5% resistance=220 package=THT]
  R14 = Resistor [tolerance=±5% resistance=220 package=THT]
  R15 = Resistor [tolerance=±5% resistance=220 package=THT]
  R16 = Resistor [tolerance=±5% resistance=220 package=THT]
  LED18 = LED - 3mm [color="Red (633nm)" package="3 mm [THT]"]
  LED19 = LED - 3mm [color="Red (633nm)" package="3 mm [THT]"]
  LED20 = LED - 3mm [color="Red (633nm)" package="3 mm [THT]"]
  LED23 = LED - 3mm [color="Red (633nm)" package="3 mm [THT]"]
  LED24 = LED - 3mm [color="Red (633nm)" package="3 mm [THT]"]
  LED21 = LED - 3mm [color="Red (633nm)" package="3 mm [THT]"]
  LED22 = LED - 3mm [color="Red (633nm)" package="3 mm [THT]"]
  LED17 = LED - 3mm [color="Red (633nm)" package="3 mm [THT]"]
  J1 = female pin header, 5 pins [form="♀ (female)"]
  J2 = female pin header, 5 pins [form="♀ (female)"]

nets:
  N1: U1.Q1, LED18.anode
  N2: U1.Q2, LED19.anode
  N3: U1.Q3, LED20.anode
  N4: U1.Q4, LED21.anode
  N5: U1.Q5, LED22.anode
  N6: U1.Q6, LED23.anode
  N7: U1.Q7, LED24.anode
  N8: U1.GND, U1.OE, R17.Pin_0, R10.Pin_0, R11.Pin_0, R12.Pin_0, R13.Pin_0, R14.Pin_0, R15.Pin_0, R16.Pin_0, J1.pin3, J2.pin3
  N9: U1.Q7', J2.pin2
  N10: U1.SH_CP, J1.pin1, J2.pin5
  N11: U1.ST_CP, J1.pin2, J2.pin4
  N12: U1.DS, J1.pin4
  N13: U1.Q0, LED17.anode
  N14: U1.VCC, J1.pin5, J2.pin1
  N15: R17.Pin_1, LED24.cathode
  N16: R10.Pin_1, LED23.cathode
  N17: R11.Pin_1, LED22.cathode
  N18: R12.Pin_1, LED21.cathode
  N19: R13.Pin_1, LED20.cathode
  N20: R14.Pin_1, LED19.cathode
  N21: R15.Pin_1, LED18.cathode
  N22: R16.Pin_1, LED17.cathode

notes:
  VCC
  data
  GRND
  latch
  clock
