# Fritzing sketch 7X8_VUMultiplex (saved by Fritzing 0.9.2b)
circuit board: 16.5cm x 8.5cm
breadboards: 1

parts:
  U1 = 74HC595 [package="DIP16 [THT]"]
  J1 = female pin header, 5 pins [form="♀ (female)"]
  R17 = Resistor [tolerance=±5% resistance=220 package=THT]
  R10 = Resistor [tolerance=±5% resistance=220 package=THT]
  R11 = Resistor [tolerance=±5% resistance=220 package=THT]
  R12 = Resistor [tolerance=±5% resistance=220 package=THT]
  R13 = Resistor [tolerance=±5% resistance=220 package=THT]
  R14 = Resistor [tolerance=±5% resistance=220 package=THT]
  R15 = Resistor [tolerance=±5% resistance=220 package=THT]
  R16 = Resistor [tolerance=±5% resistance=220 package=THT]
  LED18 = LED - 3mm [color="Red (633nm)" package="3 mm [THT]"]
  LED19 = LED - 3mm [color="Red (633nm)" package="3 mm [THT]"]
  LED20 = LED - 3mm [color="Red (633nm)" package="3 mm [THT]"]
  LED23 = LED - 3mm [color="Red (633nm)" package="3 mm [THT]"]
  LED24 = LED - 3mm [color="Red (633nm)" package="3 mm [THT]"]
  LED21 = LED - 3mm [color="Red (633nm)" package="3 mm [THT]"]
  LED22 = LED - 3mm [color="Red (633nm)" package="3 mm [THT]"]
  LED17 = LED - 3mm [color="Red (633nm)" package="3 mm [THT]"]
  LED25 = LED - 3mm [color="Red (633nm)" package="3 mm [THT]"]
  LED26 = LED - 3mm [color="Red (633nm)" package="3 mm [THT]"]
  LED27 = LED - 3mm [color="Red (633nm)" package="3 mm [THT]"]
  LED28 = LED - 3mm [color="Red (633nm)" package="3 mm [THT]"]
  LED29 = LED - 3mm [color="Red (633nm)" package="3 mm [THT]"]
  LED30 = LED - 3mm [color="Red (633nm)" package="3 mm [THT]"]
  LED31 = LED - 3mm [color="Red (633nm)" package="3 mm [THT]"]
  LED32 = LED - 3mm [color="Red (633nm)" package="3 mm [THT]"]
  U5 = 74HC595 [package="DIP16 [THT]"]
  R18 = Resistor [tolerance=±5% resistance=220 package=THT]
  R19 = Resistor [tolerance=±5% resistance=220 package=THT]
  R20 = Resistor [tolerance=±5% resistance=220 package=THT]
  R21 = Resistor [tolerance=±5% resistance=220 package=THT]
  R22 = Resistor [tolerance=±5% resistance=220 package=THT]
  R23 = Resistor [tolerance=±5% resistance=220 package=THT]
  R24 = Resistor [tolerance=±5% resistance=220 package=THT]
  R25 = Resistor [tolerance=±5% resistance=220 package=THT]
  LED33 = LED - 3mm [color="Red (633nm)" package="3 mm [THT]"]
  LED34 = LED - 3mm [color="Red (633nm)" package="3 mm [THT]"]
  LED35 = LED - 3mm [color="Red (633nm)" package="3 mm [THT]"]
  LED36 = LED - 3mm [color="Red (633nm)" package="3 mm [THT]"]
  LED37 = LED - 3mm [color="Red (633nm)" package="3 mm [THT]"]
  LED38 = LED - 3mm [color="Red (633nm)" package="3 mm [THT]"]
  LED39 = LED - 3mm [color="Red (633nm)" package="3 mm [THT]"]
  LED40 = LED - 3mm [color="Red (633nm)" package="3 mm [THT]"]
  U6 = 74HC595 [package="DIP16 [THT]"]
  R26 = Resistor [tolerance=±5% resistance=220 package=THT]
  R27 = Resistor [tolerance=±5% resistance=220 package=THT]
  R28 = Resistor [tolerance=±5% resistance=220 package=THT]
  R29 = Resistor [tolerance=±5% resistance=220 package=THT]
  R30 = Resistor [tolerance=±5% resistance=220 package=THT]
  R31 = Resistor [tolerance=±5% resistance=220 package=THT]
  R32 = Resistor [tolerance=±5% resistance=220 package=THT]
  R33 = Resistor [tolerance=±5% resistance=220 package=THT]
  LED41 = LED - 3mm [color="Red (633nm)" package="3 mm [THT]"]
  LED42 = LED - 3mm [color="Red (633nm)" package="3 mm [THT]"]
  LED43 = LED - 3mm [color="Red (633nm)" package="3 mm [THT]"]
  LED44 = LED - 3mm [color="Red (633nm)" package="3 mm [THT]"]
  LED45 = LED - 3mm [color="Red (633nm)" package="3 mm [THT]"]
  LED46 = LED - 3mm [color="Red (633nm)" package="3 mm [THT]"]
  LED47 = LED - 3mm [color="Red (633nm)" package="3 mm [THT]"]
  LED48 = LED - 3mm [color="Red (633nm)" package="3 mm [THT]"]
  U7 = 74HC595 [package="DIP16 [THT]"]
  R34 = Resistor [tolerance=±5% resistance=220 package=THT]
  R35 = Resistor [tolerance=±5% resistance=220 package=THT]
  R36 = Resistor [tolerance=±5% resistance=220 package=THT]
  R37 = Resistor [tolerance=±5% resistance=220 package=THT]
  R38 = Resistor [tolerance=±5% resistance=220 package=THT]
  R39 = Resistor [tolerance=±5% resistance=220 package=THT]
  R40 = Resistor [tolerance=±5% resistance=220 package=THT]
  R41 = Resistor [tolerance=±5% resistance=220 package=THT]
  LED49 = LED - 3mm [color="Red (633nm)" package="3 mm [THT]"]
  LED50 = LED - 3mm [color="Red (633nm)" package="3 mm [THT]"]
  LED51 = LED - 3mm [color="Red (633nm)" package="3 mm [THT]"]
  LED52 = LED - 3mm [color="Red (633nm)" package="3 mm [THT]"]
  LED53 = LED - 3mm [color="Red (633nm)" package="3 mm [THT]"]
  LED54 = LED - 3mm [color="Red (633nm)" package="3 mm [THT]"]
  LED55 = LED - 3mm [color="Red (633nm)" package="3 mm [THT]"]
  LED56 = LED - 3mm [color="Red (633nm)" package="3 mm [THT]"]
  U8 = 74HC595 [package="DIP16 [THT]"]
  R42 = Resistor [tolerance=±5% resistance=220 package=THT]
  R43 = Resistor [tolerance=±5% resistance=220 package=THT]
  R44 = Resistor [tolerance=±5% resistance=220 package=THT]
  R45 = Resistor [tolerance=±5% resistance=220 package=THT]
  R46 = Resistor [tolerance=±5% resistance=220 package=THT]
  R47 = Resistor [tolerance=±5% resistance=220 package=THT]
  R48 = Resistor [tolerance=±5% resistance=220 package=THT]
  R49 = Resistor [tolerance=±5% resistance=220 package=THT]
  LED57 = LED - 3mm [color="Red (633nm)" package="3 mm [THT]"]
  LED58 = LED - 3mm [color="Red (633nm)" package="3 mm [THT]"]
  LED59 = LED - 3mm [color="Red (633nm)" package="3 mm [THT]"]
  LED60 = LED - 3mm [color="Red (633nm)" package="3 mm [THT]"]
  LED61 = LED - 3mm [color="Red (633nm)" package="3 mm [THT]"]
  LED62 = LED - 3mm [color="Red (633nm)" package="3 mm [THT]"]
  LED63 = LED - 3mm [color="Red (633nm)" package="3 mm [THT]"]
  LED64 = LED - 3mm [color="Red (633nm)" package="3 mm [THT]"]
  U9 = 74HC595 [package="DIP16 [THT]"]
  R50 = Resistor [tolerance=±5% resistance=220 package=THT]
  R51 = Resistor [tolerance=±5% resistance=220 package=THT]
  R52 = Resistor [tolerance=±5% resistance=220 package=THT]
  R53 = Resistor [tolerance=±5% resistance=220 package=THT]
  R54 = Resistor [tolerance=±5% resistance=220 package=THT]
  R55 = Resistor [tolerance=±5% resistance=220 package=THT]
  R56 = Resistor [tolerance=±5% resistance=220 package=THT]
  R57 = Resistor [tolerance=±5% resistance=220 package=THT]
  LED65 = LED - 3mm [color="Red (633nm)" package="3 mm [THT]"]
  LED66 = LED - 3mm [color="Red (633nm)" package="3 mm [THT]"]
  LED67 = LED - 3mm [color="Red (633nm)" package="3 mm [THT]"]
  LED68 = LED - 3mm [color="Red (633nm)" package="3 mm [THT]"]
  LED69 = LED - 3mm [color="Red (633nm)" package="3 mm [THT]"]
  LED70 = LED - 3mm [color="Red (633nm)" package="3 mm [THT]"]
  LED71 = LED - 3mm [color="Red (633nm)" package="3 mm [THT]"]
  LED72 = LED - 3mm [color="Red (633nm)" package="3 mm [THT]"]
  U10 = 74HC595 [package="DIP16 [THT]"]
  R58 = Resistor [tolerance=±5% resistance=220 package=THT]
  R59 = Resistor [tolerance=±5% resistance=220 package=THT]
  R60 = Resistor [tolerance=±5% resistance=220 package=THT]
  R61 = Resistor [tolerance=±5% resistance=220 package=THT]
  R62 = Resistor [tolerance=±5% resistance=220 package=THT]
  R63 = Resistor [tolerance=±5% resistance=220 package=THT]
  R64 = Resistor [tolerance=±5% resistance=220 package=THT]
  R65 = Resistor [tolerance=±5% resistance=220 package=THT]
  J3 = female pin header, 5 pins [form="♀ (female)"]

nets:
  N1: U1.Q1, LED18.anode
  N2: U1.Q2, LED19.anode
  N3: U1.Q3, LED20.anode
  N4: U1.Q4, LED21.anode
  N5: U1.Q5, LED22.anode
  N6: U1.Q6, LED23.anode
  N7: U1.Q7, LED24.anode
  GND: U1.GND, U1.OE, J1.pin3, R17.Pin_0, R10.Pin_0, R11.Pin_0, R12.Pin_0, R13.Pin_0, R14.Pin_0, R15.Pin_0, R16.Pin_0, U5.GND, U5.OE, R18.Pin_0, R19.Pin_0, R20.Pin_0, R21.Pin_0, R22.Pin_0, R23.Pin_0, R24.Pin_0, R25.Pin_0, U6.GND, U6.OE, R27.Pin_0, R28.Pin_0, R29.Pin_0, R30.Pin_0, R31.Pin_0, R32.Pin_0, R33.Pin_0, U7.GND, U7.OE, R34.Pin_0, R35.Pin_0, R36.Pin_0, R37.Pin_0, R38.Pin_0, R39.Pin_0, R40.Pin_0, R41.Pin_0, U8.GND, U8.OE, R43.Pin_0, R44.Pin_0, R45.Pin_0, R46.Pin_0, R47.Pin_0, R48.Pin_0, R49.Pin_0, U9.GND, U9.OE, R50.Pin_0, R51.Pin_0, R52.Pin_0, R53.Pin_0, R54.Pin_0, R55.Pin_0, R56.Pin_0, R57.Pin_0, U10.GND, U10.OE, R59.Pin_0, R60.Pin_0, R61.Pin_0, R62.Pin_0, R63.Pin_0, R64.Pin_0, R65.Pin_0, J3.pin3
  N8: U1.Q7', U5.DS
  VCC: U1.MR, U1.VCC, J1.pin5, U5.MR, U5.VCC, U6.MR, U6.VCC, U7.MR, U7.VCC, U8.MR, U8.VCC, U9.MR, U9.VCC, U10.MR, U10.VCC, J3.pin5
  N9: U1.SH_CP, J1.pin1, U5.SH_CP
  N10: U1.ST_CP, J1.pin2, U5.ST_CP
  N11: U1.DS, J1.pin4
  N12: U1.Q0, LED17.anode
  N13: R17.Pin_1, LED24.cathode
  N14: R10.Pin_1, LED23.cathode
  N15: R11.Pin_1, LED22.cathode
  N16: R12.Pin_1, LED21.cathode
  N17: R13.Pin_1, LED20.cathode
  N18: R14.Pin_1, LED19.cathode
  N19: R15.Pin_1, LED18.cathode
  N20: R16.Pin_1, LED17.cathode
  N21: LED25.cathode, R18.Pin_1
  N22: LED25.anode, U5.Q0
  N23: LED26.cathode, R23.Pin_1
  N24: LED26.anode, U5.Q5
  N25: LED27.cathode, R22.Pin_1
  N26: LED27.anode, U5.Q4
  N27: LED28.cathode, R25.Pin_1
  N28: LED28.anode, U5.Q7
  N29: LED29.cathode, R24.Pin_1
  N30: LED29.anode, U5.Q6
  N31: LED30.cathode, R21.Pin_1
  N32: LED30.anode, U5.Q3
  N33: LED31.cathode, R20.Pin_1
  N34: LED31.anode, U5.Q2
  N35: LED32.cathode, R19.Pin_1
  N36: LED32.anode, U5.Q1
  N37: U5.Q7', U6.DS
  N38: LED33.cathode, R26.Pin_1
  N39: LED33.anode, U6.Q0
  N40: LED34.cathode, R31.Pin_1
  N41: LED34.anode, U6.Q5
  N42: LED35.cathode, R30.Pin_1
  N43: LED35.anode, U6.Q4
  N44: LED36.cathode, R33.Pin_1
  N45: LED36.anode, U6.Q7
  N46: LED37.cathode, R32.Pin_1
  N47: LED37.anode, U6.Q6
  N48: LED38.cathode, R29.Pin_1
  N49: LED38.anode, U6.Q3
  N50: LED39.cathode, R28.Pin_1
  N51: LED39.anode, U6.Q2
  N52: LED40.cathode, R27.Pin_1
  N53: LED40.anode, U6.Q1
  N54: U6.Q7', U7.DS
  N55: LED41.cathode, R34.Pin_1
  N56: LED41.anode, U7.Q0
  N57: LED42.cathode, R39.Pin_1
  N58: LED42.anode, U7.Q5
  N59: LED43.cathode, R38.Pin_1
  N60: LED43.anode, U7.Q4
  N61: LED44.cathode, R41.Pin_1
  N62: LED44.anode, U7.Q7
  N63: LED45.cathode, R40.Pin_1
  N64: LED45.anode, U7.Q6
  N65: LED46.cathode, R37.Pin_1
  N66: LED46.anode, U7.Q3
  N67: LED47.cathode, R36.Pin_1
  N68: LED47.anode, U7.Q2
  N69: LED48.cathode, R35.Pin_1
  N70: LED48.anode, U7.Q1
  N71: U7.Q7', U8.DS
  N72: LED49.cathode, R42.Pin_1
  N73: LED49.anode, U8.Q0
  N74: LED50.cathode, R47.Pin_1
  N75: LED50.anode, U8.Q5
  N76: LED51.cathode, R46.Pin_1
  N77: LED51.anode, U8.Q4
  N78: LED52.cathode, R49.Pin_1
  N79: LED52.anode, U8.Q7
  N80: LED53.cathode, R48.Pin_1
  N81: LED53.anode, U8.Q6
  N82: LED54.cathode, R45.Pin_1
  N83: LED54.anode, U8.Q3
  N84: LED55.cathode, R44.Pin_1
  N85: LED55.anode, U8.Q2
  N86: LED56.cathode, R43.Pin_1
  N87: LED56.anode, U8.Q1
  N88: U8.Q7', U9.DS
  N89: LED57.cathode, R50.Pin_1
  N90: LED57.anode, U9.Q0
  N91: LED58.cathode, R55.Pin_1
  N92: LED58.anode, U9.Q5
  N93: LED59.cathode, R54.Pin_1
  N94: LED59.anode, U9.Q4
  N95: LED60.cathode, R57.Pin_1
  N96: LED60.anode, U9.Q7
  N97: LED61.cathode, R56.Pin_1
  N98: LED61.anode, U9.Q6
  N99: LED62.cathode, R53.Pin_1
  N100: LED62.anode, U9.Q3
  N101: LED63.cathode, R52.Pin_1
  N102: LED63.anode, U9.Q2
  N103: LED64.cathode, R51.Pin_1
  N104: LED64.anode, U9.Q1
  N105: U9.Q7', U10.DS
  N106: U9.SH_CP, U10.SH_CP, J3.pin1
  N107: U9.ST_CP, U10.ST_CP, J3.pin2
  N108: LED65.cathode, R58.Pin_1
  N109: LED65.anode, U10.Q0
  N110: LED66.cathode, R63.Pin_1
  N111: LED66.anode, U10.Q5
  N112: LED67.cathode, R62.Pin_1
  N113: LED67.anode, U10.Q4
  N114: LED68.cathode, R65.Pin_1
  N115: LED68.anode, U10.Q7
  N116: LED69.cathode, R64.Pin_1
  N117: LED69.anode, U10.Q6
  N118: LED70.cathode, R61.Pin_1
  N119: LED70.anode, U10.Q3
  N120: LED71.cathode, R60.Pin_1
  N121: LED71.anode, U10.Q2
  N122: LED72.cathode, R59.Pin_1
  N123: LED72.anode, U10.Q1
  N124: U10.Q7', J3.pin4
