# Fritzing sketch ArduinoShield-Msgeq7-595 (saved by Fritzing 0.9.2b)
circuit board: 3.68642cm x 4.91525cm

parts:
  IC1 = MSGEQ7 DIP8 [chip_label=MSGEQ7 package="DIP (Dual Inline) [THT]"]
  IC2 = MSGEQ7 DIP8 [chip_label=MSGEQ7 package="DIP (Dual Inline) [THT]"]
  C1 = Ceramic Capacitor [capacitance=100nF package="100 mil [THT, multilayer]"]
  C2 = Ceramic Capacitor [capacitance=100nF package="100 mil [THT, multilayer]"]
  R1 = Resistor [tolerance=±5% resistance=220 package=THT]
  R2 = Resistor [tolerance=±5% resistance=220 package=THT]
  C4 = Ceramic Capacitor [capacitance=100nF package="100 mil [THT, multilayer]"]
  R4 = Resistor [tolerance=±5% resistance=220 package=THT]
  C6 = Ceramic Capacitor [capacitance=100nF package="100 mil [THT, multilayer]"]
  J1 = female pin header, 6 pins [form="♀ (female)"]
  TRS1 = Audio Jack (TRS) 3.5mm [package="4Ucon 08780 [THT]"]
  C5 = Ceramic Capacitor [capacitance=100nF package="200 mil [THT, multilayer]"]
  C3 = Ceramic Capacitor [capacitance=100nF package="200 mil [THT, multilayer]"]
  R3 = Resistor [tolerance=±5% resistance=220 package=THT]

nets:
  N1: IC1.VDDA, IC2.VDDA, R2.Pin_1, J1.pin1, R3.Pin_1
  N2: IC1.VSSA, IC2.VSSA, C1.1, C2.1, C4.1, C6.1, J1.pin2, TRS1.Sleeve
  N3: IC1.OUT, J1.pin6
  N4: IC1.STROBE, IC2.STROBE, J1.pin4
  N5: IC1.IN, C5.1
  N6: IC1.GROUND, C6.0
  N7: IC1.RESET, IC2.RESET, J1.pin3
  N8: IC1.CKIN, C4.0, R3.Pin_0
  N9: IC2.OUT, J1.pin5
  N10: IC2.IN, C3.1
  N11: IC2.GROUND, C2.0
  N12: IC2.CKIN, C1.0, R2.Pin_0
  N13: R1.Pin_0, C3.0
  N14: R1.Pin_1, TRS1.Ring
  N15: R4.Pin_0, C5.0
  N16: R4.Pin_1, TRS1.Tip

notes:
  MSGEQ7
  Stereo

custom parts:
  MSGEQ7 DIP8: MSGEQ7 DIP9=8
