# Fritzing sketch ArduinoShield-MsgeqAudioToDMX (saved by Fritzing 0.9.2b)
breadboards: 1

parts:
  MSGEQ1 = MSGEQ7 DIP8 [chip_label=MSGEQ7 package="DIP (Dual Inline) [THT]"]
  TRS1 = Audio Jack (TRS) 3.5mm [package="PG203J [THT]"]
  R3 = Resistor [tolerance=±5% resistance=200k package=THT]
  C7 = Ceramic Capacitor [capacitance=33pF package="100 mil [THT, multilayer]"]
  C8 = Ceramic Capacitor [capacitance=0.1µF package="100 mil [THT, multilayer]"]
  C9 = Ceramic Capacitor [capacitance=0.1µF package="100 mil [THT, multilayer]"]
  C10 = Ceramic Capacitor [capacitance=100nF package="100 mil [THT, multilayer]"]
  LED1 = LED - 3mm [color="Blue (430nm)" package="3 mm [THT]"]
  R4 = Resistor [tolerance=±5% resistance=220 package=THT]
  TRS2 = Audio Jack (TRS) 3.5mm [package="4Ucon 08780 [THT]"]
  U1 = MAX485 [package=dil08]
  LED3 = LED - 3mm [color="Blue (430nm)" package="3 mm [THT]"]
  LED4 = LED - 3mm [color="Blue (430nm)" package="3 mm [THT]"]
  LED5 = LED - 3mm [color="Blue (430nm)" package="3 mm [THT]"]
  LED6 = LED - 3mm [color="Blue (430nm)" package="3 mm [THT]"]
  LED7 = LED - 3mm [color="Blue (430nm)" package="3 mm [THT]"]
  LED8 = LED - 3mm [color="Blue (430nm)" package="3 mm [THT]"]  # not connected
  R5 = Resistor [tolerance=±5% resistance=220 package=THT]
  R6 = Resistor [tolerance=±5% resistance=220 package=THT]
  R7 = Resistor [tolerance=±5% resistance=220 package=THT]
  R8 = Resistor [tolerance=±5% resistance=220 package=THT]
  R9 = Resistor [tolerance=±5% resistance=220 package=THT]
  R10 = Resistor [tolerance=±5% resistance=220 package=THT]
  JP1 = Header 1 [package=1x01_offset]
  JP2 = Header 1 [package=1x01_offset]
  JP3 = Header 1 [package=1x01_offset]
  JP4 = Header 1 [package=1x01_offset]
  JP5 = Header 1 [package=1x01_offset]
  JP6 = Header 1 [package=1x01_offset]
  JP7 = Header 1 [package=1x01_offset]
  JP8 = Header 1 [package=1x01_offset]
  Composant3 = Arduino Prototyping Shield

nets (from the schematic view):
  N1: MSGEQ1.VDDA, Composant3.N$259
  N2: MSGEQ1.VSSA, Composant3.N$261
  N3: MSGEQ1.OUT, Composant3.N$262
  N4: MSGEQ1.STROBE, Composant3.N$263
  N5: MSGEQ1.IN, Composant3.N$268
  N6: MSGEQ1.GROUND, C9.0, Composant3.N$239
  N7: MSGEQ1.RESET, Composant3.N$236
  N8: MSGEQ1.CKIN, C7.1, Composant3.N$235
  N9: TRS1.Ring, Composant3.N$324, Composant3.N$325
  N10: TRS1.Tip, Composant3.N$105, Composant3.N$321
  N11: R3.Pin_0, Composant3.N$273
  N12: R3.Pin_1, C7.0, Composant3.N$231
  N13: C8.0, Composant3.N$277
  N14: C9.1, Composant3.N$240
  N15: C10.0, Composant3.N$269
  N16: C10.1, Composant3.N$305
  N17: LED1.cathode, Composant3.N$332
  N18: LED1.anode, R7.Pin_0, Composant3.N$33, Composant3.N$34
  N19: R4.Pin_0, LED6.anode, Composant3.N$178, Composant3.N$190
  N20: R4.Pin_1, Composant3.N$118
  N21: TRS2.Ring, Composant3.N$397, Composant3.N$401
  N22: TRS2.Tip, Composant3.N$189, Composant3.N$426
  N23: U1.RO, Composant3.N$403
  N24: U1.RE, Composant3.N$402
  N25: U1.DE, Composant3.N$408
  N26: U1.DI, Composant3.N$410
  N27: U1.GND, Composant3.N$53
  N28: U1.A, Composant3.N$50
  N29: U1.B, Composant3.N$51
  N30: U1.VCC, Composant3.N$117
  N31: LED3.cathode, Composant3.N$41
  N32: LED3.anode, R6.Pin_0, Composant3.N$54, Composant3.N$55
  N33: LED4.cathode, Composant3.N$84
  N34: LED4.anode, R10.Pin_0, Composant3.N$75, Composant3.N$87
  N35: LED5.cathode, Composant3.N$65
  N36: LED5.anode, R5.Pin_0, Composant3.N$78, Composant3.N$79
  N37: LED6.cathode, Composant3.N$67
  N38: LED7.cathode, Composant3.+5V
  N39: R5.Pin_1, Composant3.N$72
  N40: R6.Pin_1, Composant3.N$48
  N41: R7.Pin_1, Composant3.N$27
  N42: R8.Pin_1, Composant3.N$89
  N43: R9.Pin_1, Composant3.N$64
  N44: R10.Pin_1, Composant3.N$77
  N45: JP1.1, Composant3.N$427
  N46: JP2.1, Composant3.N$429
  N47: JP3.1, Composant3.N$431
  N48: JP4.1, Composant3.N$428
  N49: JP5.1, Composant3.N$353
  N50: JP6.1, Composant3.N$354
  N51: JP7.1, Composant3.N$356
  N52: JP8.1, Composant3.N$355

custom parts:
  MSGEQ7 DIP8: MSGEQ7 DIP9=8
