# Fritzing sketch ArduinoShield-MsgeqAudioToDMXWithScreen4 (saved by Fritzing 0.9.2b)
circuit board: 5.56842cm x 5.83297cm

parts:
  IC1 = MSGEQ7 DIP8 [chip_label=MSGEQ7 package="DIP (Dual Inline) [THT]"]
  C7 = Ceramic Capacitor [capacitance=33pF package="100 mil [THT, multilayer]"]
  C8 = Ceramic Capacitor [capacitance=100nF package="100 mil [THT, multilayer]"]
  C9 = Ceramic Capacitor [capacitance=100nF package="100 mil [THT, multilayer]"]
  C10 = Ceramic Capacitor [capacitance=10nF package="100 mil [THT, multilayer]"]
  Output_DMX = Audio Jack (TRS) 3.5mm [package="4Ucon 08780 [THT]"]
  IC2 = MAX485 [package=dil08]
  Audio_input_(mono) = Audio Jack (TRS) 3.5mm [package="PG203J [THT]"]
  R3 = Resistor [tolerance=±5% resistance=22k package=THT]
  Arduino_Shield = Arduino Prototyping Shield
  Video_out_(I2C) = Grove OLED 128x96

nets:
  VCC: IC1.VDDA, C8.1, IC2.VCC, R3.Pin_0, Arduino_Shield.+5V, Arduino_Shield.N$70, Arduino_Shield.N$94, Arduino_Shield.N$117, Arduino_Shield.N$120, Arduino_Shield.N$259, Arduino_Shield.N$283, Arduino_Shield.N$314, Video_out_(I2C).VCC
  GND: IC1.VSSA, C7.1, C8.0, C9.1, IC2.GND, Audio_input_(mono).Sleeve, Arduino_Shield.GND, Arduino_Shield.N$53, Arduino_Shield.N$232, Arduino_Shield.N$240, Arduino_Shield.N$261, Arduino_Shield.N$277, Arduino_Shield.N$293, Arduino_Shield.N$377, Arduino_Shield.N$378, Video_out_(I2C).GND
  N1: IC1.OUT, Arduino_Shield.A0, Arduino_Shield.N$262
  N2: IC1.STROBE, Arduino_Shield.D2, Arduino_Shield.N$263
  N3: IC1.IN, C10.0, Arduino_Shield.N$268, Arduino_Shield.N$269
  N4: IC1.GROUND, C9.0, Arduino_Shield.N$239
  N5: IC1.RESET, Arduino_Shield.D4, Arduino_Shield.N$236
  N6: IC1.CKIN, C7.0, R3.Pin_1, Arduino_Shield.N$168, Arduino_Shield.N$231, Arduino_Shield.N$235
  N7: C10.1, Audio_input_(mono).Tip, Arduino_Shield.N$105, Arduino_Shield.N$305, Arduino_Shield.N$321
  N8: Output_DMX.Sleeve, IC2.B, Arduino_Shield.N$51
  N9: Output_DMX.Ring, IC2.A, Arduino_Shield.N$50, Arduino_Shield.N$397
  N10: IC2.RO, Arduino_Shield.D0(RX), Arduino_Shield.N$403
  N11: IC2.RE, IC2.DE, Arduino_Shield.D13, Arduino_Shield.N$402, Arduino_Shield.N$407, Arduino_Shield.N$408
  N12: IC2.DI, Arduino_Shield.D1(TX), Arduino_Shield.N$410
  N13: Audio_input_(mono).Ring, Arduino_Shield.N$324, Arduino_Shield.N$325
  N14: Arduino_Shield.SDA, Video_out_(I2C).SDA
  N15: Arduino_Shield.SCL, Video_out_(I2C).SCL

custom parts:
  MSGEQ7 DIP8: MSGEQ7 DIP9=8
