# Fritzing sketch ArduinoShield-OpAmpAudioInput (saved by Fritzing 0.9.2b)
circuit board: 3.71019cm x 4.20249cm
breadboards: 1

parts:
  AMP = ADTL082 - Dual JFET Input Op Amps [part_number=ADTL082]
  AMP_1 = AnalogDevices_ADTL082ARZ_subpart1 [part_number=ADTL082]
  R1 = Resistor [tolerance=±5% resistance=1k package=THT]
  R2 = Resistor [tolerance=±5% resistance=220 package=THT]
  R3 = Resistor [tolerance=±5% resistance=220 package=THT]
  R4 = Resistor [tolerance=±5% resistance=220 package=THT]
  VCC1 = Battery block 9V
  Input = 3.5mm Audio Jack [package=audio-jack-3.5mm-smd]
  Output = female pin header, 2 pins [form="♀ (female)"]

nets:
  N1: AMP.connector1, AMP_1.connector1, R2.Pin_1, Output.pin1
  N2: AMP.connector2, AMP_1.connector2, R1.Pin_1, R2.Pin_0
  N3: AMP.connector3, AMP_1.connector3, R3.Pin_1, R4.Pin_0
  GND: AMP.connector4, AMP_1.connector4, Input.SLEEVE, Output.pin2
  N4: AMP.connector8, AMP_1.connector8, R3.Pin_0, VCC1.+
  N5: R1.Pin_0, Input.RIGHT
  N6: R4.Pin_1, VCC1.-
