# Fritzing sketch AudioInput (saved by Fritzing 0.9.2b)

parts:
  U3 = ADTL082 - Dual JFET Input Op Amps [part_number=ADTL082]  # not connected
  U3_1 = AnalogDevices_ADTL082ARZ_subpart1 [part_number=ADTL082]
  IC1 = MSGEQ7 [package=soic8]  # not connected
  U4 = 3.5mm Audio Jack [package=audio-jack]
  Composant1 = Arduino Uno (Rev3) - ICSP

nets:
  N1: U3_1.connector1, Composant1.A0
  N2: U3_1.connector2, U4.LEFT
  N3: U3_1.connector4, U4.SLEEVE
  N4: U3_1.connector8, Composant1.5V
