# Fritzing sketch AudioInput2 (saved by Fritzing 0.9.2b)
circuit board: 2cm x 2cm
breadboards: 1

parts:
  C1 = Electrolytic Capacitor [capacitance=10μF package="100 mil [THT, electrolytic]"]
  J3 = female pin header, 3 pins [form="♀ (female)"]
  C2 = Electrolytic Capacitor [capacitance=10μF package="100 mil [THT, electrolytic]"]
  U1 = 3.5mm Audio Jack [package=audio-jack]

nets:
  N1: C1.-, J3.pin2, C2.-, U1.SLEEVE
  N2: C1.+, J3.pin1, U1.LEFT
  N3: J3.pin3, C2.+, U1.RIGHT
