# Fritzing sketch DrumLightsShield-V1 (saved by Fritzing 0.9.3b)
circuit board: 6.46975cm x 5.4371cm
breadboards: 1

parts:
  U1 = RJ45 Jack [package=rj45-8]
  Composant1 = Arduino Uno (Rev3) - ICSP
  U2 = RJ45 Jack [package=rj45-8]
  U3 = RJ45 Jack [package=rj45-8]
  U4 = RJ45 Jack [package=rj45-8]
  U5 = RJ45 Jack [package=rj45-8]
  U6 = RJ45 Jack [package=rj45-8]

nets:
  N1: U1.1, U1.2, Composant1.5V, U2.1, U2.2, U3.1, U3.2, U4.1, U4.2, U5.1, U5.2, U6.1, U6.2
  N2: U1.3, U1.4, U1.5, Composant1.GND, U2.3, U2.4, U2.5, U4.3, U4.4, U4.5
  N3: U1.6, Composant1.A4/SDA
  N4: U1.7, U2.8
  N5: U1.8, Composant1.D2
  N6: Composant1.A0, U3.6
  N7: Composant1.A1, U6.6
  N8: Composant1.A2, U5.6
  N9: Composant1.A3, U4.6
  N10: Composant1.A5/SCL, U2.6
  N11: U2.7, U6.8
  N12: U3.3, U3.4, U3.5, U5.3, U5.4, U5.5, U6.3, U6.4, U6.5
  N13: U3.7, U5.8
  N14: U3.8, U6.7
  N15: U4.8, U5.7
