# Fritzing sketch LED_VU (saved by Fritzing 0.9.2b)
circuit board: 7.70128cm x 10.8062cm

parts:
  Composant1 = Arduino Uno (Rev3) - ICSP  # not connected
  U5 = 74HC595 SMD [package="SO16 [SMD]"]
  LED3 = LEDs [package=led10mm]
  LED4 = LEDs [package=led10mm]
  LED5 = LEDs [package=led10mm]
  LED6 = LEDs [package=led10mm]
  LED7 = LEDs [package=led10mm]
  LED8 = LEDs [package=led10mm]
  LED9 = LEDs [package=led10mm]
  LED10 = LEDs [package=led10mm]
  R1 = Resistor [tolerance=±5% resistance=220 package=THT]
  R2 = Resistor [tolerance=±5% resistance=220 package=THT]
  R3 = Resistor [tolerance=±5% resistance=220 package=THT]
  R4 = Resistor [tolerance=±5% resistance=220 package=THT]
  R5 = Resistor [tolerance=±5% resistance=220 package=THT]
  R6 = Resistor [tolerance=±5% resistance=220 package=THT]
  R7 = Resistor [tolerance=±5% resistance=220 package=THT]
  R8 = Resistor [tolerance=±5% resistance=220 package=THT]
  J1 = female pin header, 2 pins [form="♀ (female)"]
  J3 = female pin header, 3 pins [form="♀ (female)"]

nets:
  N1: U5.Q1, R1.Pin_1
  N2: U5.Q2, R2.Pin_1
  N3: U5.Q3, R3.Pin_1
  N4: U5.Q4, R4.Pin_1
  N5: U5.Q5, R5.Pin_1
  N6: U5.Q6, R6.Pin_1
  N7: U5.Q7, R7.Pin_1
  N8: U5.MR, U5.VCC, J1.pin1
  N9: U5.SH_CP, J3.pin3
  N10: U5.ST_CP, J3.pin2
  N11: U5.OE, LED3.C, LED4.C, LED5.C, LED6.C, LED7.C, LED8.C, LED9.C, LED10.C, J1.pin2
  N12: U5.DS, J3.pin1
  N13: U5.Q0, R8.Pin_1
  N14: LED3.A, R1.Pin_0
  N15: LED4.A, R2.Pin_0
  N16: LED5.A, R3.Pin_0
  N17: LED6.A, R4.Pin_0
  N18: LED7.A, R5.Pin_0
  N19: LED8.A, R6.Pin_0
  N20: LED9.A, R7.Pin_0
  N21: LED10.A, R8.Pin_0
