# Fritzing sketch MSGEQ7 (saved by Fritzing 0.9.2b)
circuit board: 8.46667cm x 5.64444cm
breadboards: 1

parts:
  IC1 = MSGEQ7 [package=soic8]
  U1 = AUDIO-JACK2 [package=audio-jack-3.5mm-smd]
  C1 = Ceramic Capacitor [capacitance="100 nF" package="0805 [SMD, multilayer]"]
  C2 = Capacitor [package=cap-pth-small-kit]
  C3 = Ceramic Capacitor [capacitance="100 nF" package="0805 [SMD, multilayer]"]
  C4 = Ceramic Capacitor [capacitance="100 nF" package="0805 [SMD, multilayer]"]
  R1 = Resistor [tolerance=±5% resistance=220 package=THT]
  U2 = atmega328 [package=dip]

nets:
  N1: IC1.VDD, C2.1, R1.Pin_0, U2.AVCC
  N2: IC1.GND, U1.SLEEVE, C2.2, C3.1, C4.0, U2.GND#21
  N3: IC1.DCOUT, U2.A0
  N4: IC1.STROBE, U2.D8
  N5: IC1.AUDIO_IN, C1.0
  N6: IC1.CG, C3.0
  N7: IC1.RESET, U2.D10_(PWM)
  N8: IC1.CKIN, C4.1, R1.Pin_1
  N9: U1.TIP, C1.1
