# Fritzing sketch Mp3Doorbell (saved by Fritzing 0.9.2b)
circuit board: 8.46667cm x 5.64444cm

parts:
  Wifi = ESP8266 WiFi Module [part_number=ESP8266]
  Composant1 = Arduino Nano (Rev3.0)
  Mp3_Player = WTV020SD [package=ssop_20]
  S2 = Round Pushbutton
  S3 = Round Pushbutton
  16v_input_from_transformer_(120_VAC_to_16_DC) = Power plug
  16v_to_9v = Voltage Regulator - Variable [package="TO220 [THT]"]
  U1 = Voltage Regulator - 3.3V [package="TO220 [THT]"]
  SP1 = SPEAKER [package=pcb_mount_speaker]
  R1 = Trimmer Potentiometer [maximum_resistance=10kΩ package=THT]

nets:
  N1: Wifi.RXD, Composant1.D1/TX
  VCC: Wifi.VCC, Mp3_Player.VCC, U1.output_voltage
  GND: Wifi.GND, Composant1.GND, Mp3_Player.GND, S2.leg0, S3.leg0, 16v_input_from_transformer_(120_VAC_to_16_DC).GND, U1.GND, R1.wiper
  N2: Wifi.TXD, Composant1.D0/RX
  N3: Composant1.VIN, 16v_to_9v.OUT
  N4: Composant1.A1, S3.leg1
  N5: Composant1.A0, S2.leg1
  N6: Mp3_Player.SPK_P, SP1.-
  N7: Mp3_Player.SPK_N, SP1.+
  N8: 16v_input_from_transformer_(120_VAC_to_16_DC).VCC, 16v_to_9v.IN, U1.input_voltage
  N9: 16v_to_9v.ADJ, R1.leg2

custom parts:
  ESP8266 WiFi Module: Generic WiFi Module based on the ESP8266 with onboard PCB antenna and UART communications
